// Logisim project processor.circ as structural Verilog: 8 circuits, main circuit main
module main (
  output [7:0] out_1
);

  wire and_2_out, Clear, Clear_Memory_out, Clock, clock_1_out, Enable, MemSrc, or_1_out;
  wire [2:0] instruction_divider_1_rd, instruction_divider_1_rs, instruction_divider_1_rt, multiplexer_1_out;
  wire [3:0] instruction_memory_1_out_5, registers_1_selected_register_output,
       registers_1_selected_register_output_2;
  wire [4:0] instruction_divider_1_opcode;
  wire [7:0] alu_1_output, instruction_divider_1_immediate, memory_1_dataread, multiplexer_2_out,
       multiplexer_3_out, multiplexer_4_out, registers_1_rd_rs_data_output, registers_1_rt_data_output;
  wire [7:4] instruction_memory_1_out_5_2;
  wire [15:0] instruction_memory_1_instruction;

  Clock clock_1 (.out(clock_1_out));
  Button button_1 (.out(Clear));
  Hex_Digit_Display hex_digit_display_1 (.value(instruction_memory_1_out_5_2));  // open: dp
  and and_1 (Clock, clock_1_out, Enable);
  Hex_Digit_Display hex_digit_display_2 (.value(instruction_memory_1_out_5));  // open: dp
  or or_1 (or_1_out, and_2_out, out_1[6]);
  Hex_Digit_Display hex_digit_display_3 (.value(registers_1_selected_register_output_2));  // open: dp
  Instruction_Memory instruction_memory_1 (
    .Clock(Clock), .Clear(Clear), .Instruction(instruction_memory_1_instruction), .Jump(or_1_out),
    .Address(instruction_divider_1_immediate),
    .out_5({instruction_memory_1_out_5_2, instruction_memory_1_out_5}));
  and and_2 (and_2_out, out_1[5], alu_1_output[0]);
  Hex_Digit_Display hex_digit_display_4 (.value(registers_1_selected_register_output));  // open: dp
  Instruction_Divider instruction_divider_1 (
    .Instruction(instruction_memory_1_instruction), .Immediate(instruction_divider_1_immediate),
    .Rs(instruction_divider_1_rs), .Rd(instruction_divider_1_rd), .Opcode(instruction_divider_1_opcode),
    .Rt(instruction_divider_1_rt));
  Control2 control2_1 (
    .a(instruction_divider_1_opcode[4]), .WriteReg(out_1[7]), .b(instruction_divider_1_opcode[3]),
    .c(instruction_divider_1_opcode[2]), .d(instruction_divider_1_opcode[1]),
    .e(instruction_divider_1_opcode[0]), .Jump(out_1[6]), .Branch(out_1[5]), .ALUSrc(out_1[4]),
    .MemStore(out_1[1]), .MemReg(out_1[0]), .Finish(Enable), .MemSrc(MemSrc), .out_10(out_1[3:2]));
  Multiplexer #(.width(3)) multiplexer_1 (
    .in0(instruction_divider_1_rt), .in1(instruction_divider_1_immediate[2:0]), .out(multiplexer_1_out),
    .sel(MemSrc), .en(1'b1));
  Registers registers_1 (
    .in_1(Clock), .RD_Register(instruction_divider_1_rd), .in_3(Clear), .in_5(out_1[7]),
    .Data_Input(multiplexer_4_out), .Rd_Rs_Data_output(registers_1_rd_rs_data_output),
    .RS_Register(instruction_divider_1_rs), .Rt_Data_output(registers_1_rt_data_output),
    .RT_Register(multiplexer_1_out), .DataSrc(out_1[4]),
    .Selected_Register_output({registers_1_selected_register_output_2, registers_1_selected_register_output}));
  Multiplexer #(.width(8)) multiplexer_2 (
    .in0(registers_1_rt_data_output), .in1(instruction_divider_1_immediate), .out(multiplexer_2_out),
    .sel(out_1[4]), .en(1'b1));
  Multiplexer #(.width(8)) multiplexer_3 (
    .in0(instruction_divider_1_immediate), .in1(registers_1_rt_data_output), .out(multiplexer_3_out),
    .sel(MemSrc), .en(1'b1));
  ALU alu_1 (
    .A(registers_1_rd_rs_data_output), .B(multiplexer_2_out), .ALUOp(out_1[3:2]), .Output(alu_1_output),
    .Branch(out_1[5]));
  Memory memory_1 (
    .DataStored(registers_1_rd_rs_data_output), .Load_Store(out_1[1]), .Address(multiplexer_3_out),
    .Enable(1'b1), .Clock(Clock), .Clear(Clear_Memory_out), .DataRead(memory_1_dataread));
  Button Clear_Memory (.out(Clear_Memory_out));
  Multiplexer #(.width(8)) multiplexer_4 (
    .in0(alu_1_output), .in1(memory_1_dataread), .out(multiplexer_4_out), .sel(out_1[0]), .en(1'b1));

  // Other names for the same wires on the sheet: MemReg = out_1[0]; MemStore = out_1[1]; ALUOp[1:0] = out_1[3:2];
  //   ALUSrc = out_1[4]; Branch = out_1[5]; Jump = out_1[6]; RegWrite = out_1[7]
endmodule

module Instruction_Memory (
  input  Jump,
  input  [7:0] Address,
  input  Clock,
  input  Clear,
  output [7:0] out_5,
  output [15:0] Instruction
);

  wire [7:0] adder_1_out, multiplexer_1_out;

  Multiplexer #(.width(8)) multiplexer_1 (
    .in0(adder_1_out), .in1(Address), .out(multiplexer_1_out), .sel(Jump), .en(1'b1));
  Register PC (.D(multiplexer_1_out), .en(1'b1), .Q(out_5), .clk(Clock), .clr(Clear));
  Adder adder_1 (.a(out_5), .b(8'h1), .out(adder_1_out));  // open: cin, cout
  ROM #(.dataWidth(16)) rom_1 (.addr(out_5), .data(Instruction), .sel(1'b1));

  // Notes on the sheet:
  //   contents of rom_1 (hex, n*v repeats v):
  //   1800 1f04 a900 1801 aa00 16e0 460e 1544 450b 29ff 128 1801 aa00 3805 1900 f900
endmodule

module Registers (
  input  in_1,
  input  [2:0] RD_Register,
  input  in_3,
  input  DataSrc,
  input  in_5,
  input  [2:0] RS_Register,
  input  [2:0] RT_Register,
  input  [7:0] Data_Input,
  output [7:0] Rd_Rs_Data_output,
  output [7:0] Selected_Register_output,
  output [7:0] Rt_Data_output
);

  wire R1, R2, R3, R4, R5, R6, R7, R8;
  wire [2:0] multiplexer_2_out;
  wire [7:0] demultiplexer_2_out0, demultiplexer_2_out1, demultiplexer_2_out2, demultiplexer_2_out3,
       demultiplexer_2_out4, demultiplexer_2_out5, demultiplexer_2_out6, demultiplexer_2_out7, register_1_q,
       register_2_q, register_3_q, register_4_q, register_5_q, register_6_q, register_7_q, register_8_q;

  Demultiplexer #(.select(3)) demultiplexer_1 (
    .out0(R1), .out1(R2), .out2(R3), .out3(R4), .out4(R5), .out5(R6), .out6(R7), .out7(R8), .in(in_5),
    .sel(RD_Register), .en(1'b1));
  Demultiplexer #(.select(3), .width(8)) demultiplexer_2 (
    .out0(demultiplexer_2_out0), .out1(demultiplexer_2_out1), .out2(demultiplexer_2_out2),
    .out3(demultiplexer_2_out3), .out4(demultiplexer_2_out4), .out5(demultiplexer_2_out5),
    .out6(demultiplexer_2_out6), .out7(demultiplexer_2_out7), .in(Data_Input), .sel(RD_Register), .en(1'b1));
  Register register_1 (.D(demultiplexer_2_out0), .en(R1), .Q(register_1_q), .clk(in_1), .clr(in_3));
  Register register_2 (.D(demultiplexer_2_out1), .en(R2), .Q(register_2_q), .clk(in_1), .clr(in_3));
  Register register_3 (.D(demultiplexer_2_out2), .en(R3), .Q(register_3_q), .clk(in_1), .clr(in_3));
  Register register_4 (.D(demultiplexer_2_out3), .en(R4), .Q(register_4_q), .clk(in_1), .clr(in_3));
  Register register_5 (.D(demultiplexer_2_out4), .en(R5), .Q(register_5_q), .clk(in_1), .clr(in_3));
  Register register_6 (.D(demultiplexer_2_out5), .en(R6), .Q(register_6_q), .clk(in_1), .clr(in_3));
  Register register_7 (.D(demultiplexer_2_out6), .en(R7), .Q(register_7_q), .clk(in_1), .clr(in_3));
  Register register_8 (.D(demultiplexer_2_out7), .en(R8), .Q(register_8_q), .clk(in_1), .clr(in_3));
  Multiplexer #(.select(3), .width(8)) multiplexer_1 (
    .in0(register_1_q), .in1(register_2_q), .in2(register_3_q), .in3(register_4_q), .in4(register_5_q),
    .in5(register_6_q), .in6(register_7_q), .in7(register_8_q), .out(Rd_Rs_Data_output),
    .sel(multiplexer_2_out), .en(1'b1));
  Multiplexer #(.width(3)) multiplexer_2 (
    .in0(RS_Register), .in1(RD_Register), .out(multiplexer_2_out), .sel(DataSrc), .en(1'b1));
  Multiplexer #(.select(3), .width(8)) multiplexer_3 (
    .in0(register_1_q), .in1(register_2_q), .in2(register_3_q), .in3(register_4_q), .in4(register_5_q),
    .in5(register_6_q), .in6(register_7_q), .in7(register_8_q), .out(Rt_Data_output), .sel(RT_Register),
    .en(1'b1));

  assign Selected_Register_output = Rd_Rs_Data_output;

  // Other names for the same wires on the sheet: Clear = in_3; Clock = in_1; Rd[2:0] = RD_Register; RegWrite = in_5;
  //   Rs[2:0] = RS_Register; Rt[2:0] = RT_Register
endmodule

module Instruction_Divider (
  input  [15:0] Instruction,
  output [7:0] Immediate,
  output [2:0] Rt,
  output [2:0] Rs,
  output [2:0] Rd,
  output [4:0] Opcode
);


  assign Immediate = Instruction[7:0];
  assign Opcode = Instruction[15:11];
  assign Rd = Instruction[10:8];
  assign Rs = Instruction[7:5];
  assign Rt = Instruction[4:2];
endmodule

module ALU (
  input  [7:0] A,
  input  [7:0] B,
  input  [1:0] ALUOp,
  input  Branch,
  output [7:0] Output
);

  wire [0:0] comparator_1_eq, comparator_1_lt;
  wire [7:0] adder_1_out, multiplexer_1_out, subtractor_1_out;

  Multiplexer #(.width(8)) multiplexer_1 (.in0(B), .in1(8'h1), .out(multiplexer_1_out), .sel(Branch), .en(1'b1));
  Adder adder_1 (.a(A), .b(B), .out(adder_1_out));  // open: cin, cout
  Subtractor subtractor_1 (.a(A), .b(B), .out(subtractor_1_out));  // open: bin, bout
  Comparator comparator_1 (.a(A), .b(multiplexer_1_out), .eq(comparator_1_eq[0]), .lt(comparator_1_lt[0]));  // open: gt
  Multiplexer #(.select(2), .width(8)) multiplexer_2 (
    .in0(adder_1_out), .in1(subtractor_1_out), .in2({{7{1'b0}}, comparator_1_eq[0]}),
    .in3({{7{1'b0}}, comparator_1_lt[0]}), .out(Output), .sel(ALUOp), .en(1'b1));

  // Other names for the same wires on the sheet: Bit_0 = ALUOp[0]; Bit_1 = ALUOp[1]
endmodule

module Control (
  input  [4:0] in_1,
  output [1:0] ALUOp,
  output WriteReg,
  output Jump,
  output Branch,
  output ALUSrc,
  output MemStore,
  output MemReg,
  output Enable
);

  wire and_1_out, and_2_out, and_3_out, and_4_out, and_5_out, and_6_out, and_7_out, and_8_out, and_9_out,
       and_10_out, and_11_out, and_12_out, and_13_out, and_14_out, and_15_out, and_16_out, and_17_out,
       and_18_out, and_19_out, and_20_out, and_21_out, and_22_out, and_23_out, and_24_out, and_25_out,
       and_26_out, and_27_out, and_28_out, and_29_out, and_30_out, not_2_out, not_3_out, not_4_out,
       not_5_out, not_6_out, not_7_out, not_8_out, not_9_out, not_10_out, not_11_out, not_12_out, not_13_out,
       not_14_out, not_15_out, not_16_out, not_17_out, not_18_out, not_19_out, not_20_out, not_21_out,
       not_22_out, not_23_out, not_24_out, not_25_out, not_26_out, not_27_out, not_28_out, not_29_out,
       not_30_out, not_31_out, not_32_out, not_33_out, not_34_out, not_35_out, not_36_out, not_37_out,
       not_38_out;

  and and_1 (and_1_out, in_1[4], in_1[3], in_1[2], in_1[1], in_1[0]);
  not not_1 (Enable, and_1_out);
  not not_2 (not_2_out, in_1[4]);
  not not_3 (not_3_out, in_1[3]);
  not not_4 (not_4_out, in_1[1]);
  not not_5 (not_5_out, in_1[2]);
  not not_6 (not_6_out, in_1[2]);
  not not_7 (not_7_out, in_1[1]);
  not not_8 (not_8_out, in_1[0]);
  not not_9 (not_9_out, in_1[2]);
  not not_10 (not_10_out, in_1[4]);
  not not_11 (not_11_out, in_1[2]);
  not not_12 (not_12_out, in_1[1]);
  not not_13 (not_13_out, in_1[0]);
  not not_14 (not_14_out, in_1[4]);
  not not_15 (not_15_out, in_1[2]);
  not not_16 (not_16_out, in_1[1]);
  not not_17 (not_17_out, in_1[0]);
  not not_18 (not_18_out, in_1[4]);
  not not_19 (not_19_out, in_1[3]);
  not not_20 (not_20_out, in_1[4]);
  not not_21 (not_21_out, in_1[2]);
  not not_22 (not_22_out, in_1[1]);
  not not_23 (not_23_out, in_1[0]);
  not not_24 (not_24_out, in_1[0]);
  not not_25 (not_25_out, in_1[4]);
  not not_26 (not_26_out, in_1[0]);
  not not_27 (not_27_out, in_1[1]);
  not not_28 (not_28_out, in_1[0]);
  not not_29 (not_29_out, in_1[4]);
  not not_30 (not_30_out, in_1[3]);
  not not_31 (not_31_out, in_1[4]);
  not not_32 (not_32_out, in_1[3]);
  not not_33 (not_33_out, in_1[0]);
  not not_34 (not_34_out, in_1[1]);
  not not_35 (not_35_out, in_1[1]);
  not not_36 (not_36_out, in_1[4]);
  not not_37 (not_37_out, in_1[1]);
  not not_38 (not_38_out, in_1[0]);
  and and_2 (and_2_out, not_2_out, not_3_out, not_4_out);
  and and_3 (and_3_out, not_5_out, in_1[0]);
  and and_4 (and_4_out, not_6_out, in_1[1]);
  and and_5 (and_5_out, in_1[2], not_7_out, not_8_out);
  and and_6 (and_6_out, in_1[4], not_9_out);
  and and_7 (and_7_out, in_1[2], in_1[1], in_1[0]);
  and and_8 (and_8_out, not_10_out, in_1[3], not_11_out, not_12_out, not_13_out);
  and and_9 (and_9_out, in_1[3], in_1[2], in_1[1]);
  and and_10 (and_10_out, in_1[4], in_1[2], in_1[1]);
  and and_11 (and_11_out, not_14_out, in_1[3], not_15_out, not_16_out, not_17_out);
  and and_12 (and_12_out, in_1[3], in_1[2], in_1[1], in_1[0]);
  and and_13 (and_13_out, in_1[4], in_1[2], in_1[1], in_1[0]);
  and and_14 (and_14_out, in_1[1], in_1[0]);
  and and_15 (and_15_out, not_18_out, not_19_out, in_1[2]);
  and and_16 (and_16_out, not_20_out, in_1[3], not_21_out, not_22_out, not_23_out);
  and and_17 (and_17_out, in_1[1], not_24_out);
  and and_18 (and_18_out, not_25_out, in_1[3], not_26_out);
  and and_19 (and_19_out, in_1[3], in_1[2]);
  and and_20 (and_20_out, in_1[4], in_1[2]);
  and and_21 (and_21_out, not_27_out, in_1[0]);
  and and_22 (and_22_out, in_1[1], not_28_out);
  and and_23 (and_23_out, not_29_out, not_30_out, in_1[2]);
  and and_24 (and_24_out, not_31_out, not_32_out, in_1[2], in_1[1], not_33_out);
  and and_25 (and_25_out, in_1[3], in_1[2], not_34_out, in_1[0]);
  and and_26 (and_26_out, in_1[4], in_1[2], not_35_out, in_1[0]);
  and and_27 (and_27_out, in_1[2], in_1[0]);
  and and_28 (and_28_out, not_36_out, in_1[3], not_37_out, not_38_out);
  and and_29 (and_29_out, in_1[3], in_1[2]);
  and and_30 (and_30_out, in_1[4], in_1[2]);
  or or_1 (WriteReg, and_2_out, and_3_out, and_4_out, and_5_out, and_6_out);
  or or_2 (Jump, and_7_out, and_8_out, and_9_out, and_10_out);
  or or_3 (Branch, and_11_out, and_12_out, and_13_out);
  or or_4 (ALUSrc, and_14_out, and_15_out, and_16_out);
  or or_5 (ALUOp[1], and_17_out, and_18_out, and_19_out, and_20_out);
  or or_6 (ALUOp[0], and_21_out, and_22_out, and_23_out);
  or or_7 (MemStore, and_24_out, and_25_out, and_26_out);
  or or_8 (MemReg, and_27_out, and_28_out, and_29_out, and_30_out);
endmodule

module Memory (
  input  [7:0] DataStored,
  input  Load_Store,
  input  [7:0] Address,
  input  Enable,
  input  Clock,
  input  Clear,
  output [7:0] DataRead
);

  wire not_1_out;

  assign DataRead = Load_Store ? DataStored : 8'bz;  // Controlled_Buffer controlled_buffer_1
  not not_1 (not_1_out, Load_Store);
  RAM ram_1 (.addr(Address), .data(DataRead), .sel(Enable), .clk(Clock), .ld(not_1_out), .clr(Clear));
endmodule

// Control
module Control2 (
  input  a,
  input  b,
  input  c,
  input  d,
  input  e,
  output WriteReg,
  output Jump,
  output Branch,
  output ALUSrc,
  output [1:0] out_10,
  output MemStore,
  output MemReg,
  output Finish,
  output MemSrc
);

  wire and_1_out, and_2_out, and_3_out, and_4_out, and_5_out, and_6_out, and_7_out, and_8_out, and_9_out,
       and_10_out, and_11_out, and_12_out, and_13_out, and_14_out, and_15_out, and_16_out, and_17_out,
       and_19_out, and_20_out, and_21_out, and_22_out, and_23_out, and_24_out, and_25_out, not_1_out,
       not_2_out, not_3_out, not_4_out, not_5_out, not_6_out, not_7_out, not_8_out, not_9_out, not_10_out,
       not_11_out, not_12_out, not_13_out, not_14_out, not_15_out, not_16_out, not_17_out, not_18_out,
       not_19_out, not_20_out, not_21_out, not_22_out, not_23_out, not_24_out, not_25_out, not_26_out;

  not not_1 (not_1_out, b);
  not not_2 (not_2_out, c);
  not not_3 (not_3_out, b);
  not not_4 (not_4_out, d);
  not not_5 (not_5_out, b);
  not not_6 (not_6_out, a);
  not not_7 (not_7_out, a);
  not not_8 (not_8_out, a);
  not not_9 (not_9_out, c);
  not not_10 (not_10_out, d);
  not not_11 (not_11_out, e);
  not not_12 (not_12_out, a);
  not not_13 (not_13_out, c);
  not not_14 (not_14_out, d);
  not not_15 (not_15_out, e);
  and and_1 (and_1_out, d, e);
  not not_16 (not_16_out, e);
  not not_17 (not_17_out, d);
  not not_18 (not_18_out, e);
  not not_19 (not_19_out, e);
  not not_20 (not_20_out, a);
  not not_21 (not_21_out, b);
  not not_22 (not_22_out, d);
  nand nand_1 (Finish, a, b);
  not not_23 (not_23_out, b);
  not not_24 (not_24_out, c);
  not not_25 (not_25_out, d);
  not not_26 (not_26_out, e);
  and and_2 (and_2_out, not_1_out, not_2_out);
  and and_3 (and_3_out, not_3_out, not_4_out);
  and and_4 (and_4_out, not_5_out, c, d, e);
  and and_5 (and_5_out, not_6_out, b, e);
  and and_6 (and_6_out, not_7_out, b, d);
  and and_7 (and_7_out, not_8_out, b, c);
  and and_8 (and_8_out, a, b, not_9_out);
  and and_9 (and_9_out, a, b, not_10_out);
  and and_10 (and_10_out, a, b, not_11_out);
  and and_11 (and_11_out, not_12_out, b);
  and and_12 (and_12_out, b, not_13_out);
  and and_13 (and_13_out, b, not_14_out);
  and and_14 (and_14_out, b, not_15_out);
  or or_1 (ALUSrc, and_1_out, c, b);
  and and_15 (and_15_out, d, not_16_out);
  and and_16 (and_16_out, not_17_out, e);
  and and_17 (and_17_out, d, not_18_out);
  and and_18 (MemStore, c, d, not_19_out);
  and and_19 (and_19_out, not_20_out, c, e);
  and and_20 (and_20_out, not_21_out, c, e);
  and and_21 (and_21_out, c, not_22_out, e);
  and and_22 (and_22_out, a, not_23_out);
  and and_23 (and_23_out, a, not_24_out);
  and and_24 (and_24_out, a, not_25_out);
  and and_25 (and_25_out, a, not_26_out);
  or or_2 (WriteReg, and_2_out, and_3_out);
  or or_3 (Jump, and_4_out, and_5_out, and_6_out, and_7_out, and_8_out, and_9_out, and_10_out);
  or or_4 (Branch, and_11_out, and_12_out, and_13_out, and_14_out);
  or or_5 (out_10[1], and_15_out, b);
  or or_6 (out_10[0], and_16_out, and_17_out, c);
  or or_7 (MemReg, and_19_out, and_20_out, and_21_out);
  or or_8 (MemSrc, and_22_out, and_23_out, and_24_out, and_25_out);
endmodule
